// Logisim project CPU.circ as structural Verilog: 4 circuits, main circuit main
module main (
  input  [7:0] in_1,
  input  in_2,
  input  in_3,
  input  in_4,
  input  in_5,
  input  in_6,
  output [7:0] out_7
);

  wire clock_1_out;
  wire [7:0] d38_1_o, register_1_q, register_2_q, register_3_q, register_4_q, register_5_q, register_6_q,
       register_7_q, register_8_q;

  Clock clock_1 (.out(clock_1_out));
  D38 d38_1 (.En(in_3), .A0(in_4), .A1(in_5), .A2(in_6), .O(d38_1_o));
  Register register_1 (.D(in_1), .en(d38_1_o[0]), .clk(clock_1_out), .Q(register_1_q), .clr(in_2));
  Register register_2 (.D(in_1), .en(d38_1_o[1]), .clk(clock_1_out), .Q(register_2_q), .clr(in_2));
  assign out_7 = d38_1_o[0] ? register_1_q : 8'bz;  // Controlled_Buffer controlled_buffer_1
  Register register_3 (.D(in_1), .en(d38_1_o[2]), .clk(clock_1_out), .Q(register_3_q), .clr(in_2));
  assign out_7 = d38_1_o[1] ? register_2_q : 8'bz;  // Controlled_Buffer controlled_buffer_2
  assign out_7 = d38_1_o[2] ? register_3_q : 8'bz;  // Controlled_Buffer controlled_buffer_3
  Register register_4 (.D(in_1), .en(d38_1_o[3]), .clk(clock_1_out), .Q(register_4_q), .clr(in_2));
  Register register_5 (.D(in_1), .en(d38_1_o[4]), .clk(clock_1_out), .Q(register_5_q), .clr(in_2));
  assign out_7 = d38_1_o[3] ? register_4_q : 8'bz;  // Controlled_Buffer controlled_buffer_4
  assign out_7 = d38_1_o[4] ? register_5_q : 8'bz;  // Controlled_Buffer controlled_buffer_5
  Register register_6 (.D(in_1), .en(d38_1_o[5]), .clk(clock_1_out), .Q(register_6_q), .clr(in_2));
  assign out_7 = d38_1_o[5] ? register_6_q : 8'bz;  // Controlled_Buffer controlled_buffer_6
  Register register_7 (.D(in_1), .en(d38_1_o[6]), .clk(clock_1_out), .Q(register_7_q), .clr(in_2));
  Register register_8 (.D(in_1), .en(d38_1_o[7]), .clk(clock_1_out), .Q(register_8_q), .clr(in_2));
  assign out_7 = d38_1_o[6] ? register_7_q : 8'bz;  // Controlled_Buffer controlled_buffer_7
endmodule

module D38 (
  input  En,
  input  A0,
  input  A1,
  input  A2,
  output [7:0] O
);

  wire not_1_out, not_2_out, not_3_out;

  not not_1 (not_1_out, A2);
  not not_2 (not_2_out, A1);
  not not_3 (not_3_out, A0);
  and and_1 (O[0], not_3_out, not_2_out, not_1_out, En);
  and and_2 (O[1], A0, not_2_out, not_1_out, En);
  and and_3 (O[2], not_3_out, A1, not_1_out, En);
  and and_4 (O[3], A0, A1, not_1_out, En);
  and and_5 (O[4], not_3_out, not_2_out, A2, En);
  and and_6 (O[5], A0, not_2_out, A2, En);
  and and_7 (O[6], not_3_out, A1, A2, En);
  and and_8 (O[7], A0, A1, A2, En);
endmodule

module Marquee (
  output out_1,
  output out_2,
  output out_3,
  output out_4
);

  wire clock_1_out, not_1_out, or_1_out;

  Clock clock_1 (.out(clock_1_out));
  D_Flip_Flop d_ff_1 (.D(out_1), .clk(clock_1_out), .Q(out_2));  // open: Qn, preset, reset
  D_Flip_Flop d_ff_2 (.D(not_1_out), .clk(clock_1_out), .Q(out_1));  // open: Qn, preset, reset
  D_Flip_Flop d_ff_3 (.D(out_2), .clk(clock_1_out), .Q(out_3));  // open: Qn, preset, reset
  D_Flip_Flop d_ff_4 (.D(out_3), .clk(clock_1_out), .Q(out_4));  // open: Qn, preset, reset
  or or_1 (or_1_out, out_1, out_2, out_3);
  not not_1 (not_1_out, or_1_out);
endmodule

module Count (
  input  in_1,
  output out_2,
  output out_3,
  output out_4,
  output out_5
);

  wire clock_1_out;
  wire [3:0] negator_1_out;

  Clock clock_1 (.out(clock_1_out));
  T_Flip_Flop t_ff_1 (.T(out_2), .clk(out_2), .Q(out_3));  // open: Qn, reset, preset
  T_Flip_Flop t_ff_2 (.T(in_1), .clk(clock_1_out), .Q(out_2));  // open: Qn, reset, preset
  T_Flip_Flop t_ff_3 (.T(out_3), .clk(out_3), .Q(out_4));  // open: Qn, reset, preset
  T_Flip_Flop t_ff_4 (.T(out_4), .clk(out_4), .Q(out_5));  // open: Qn, reset, preset
  Hex_Digit_Display #(.decimalPoint("false")) hex_digit_display_1 (.value(negator_1_out));
  Negator #(.width(4)) negator_1 (.in({out_5, out_4, out_3, out_2}), .out(negator_1_out));
endmodule
